// Logisim project riscv_logisim.circ as structural Verilog: 6 circuits, main circuit main
module main (
  input  [31:0] in_1
);

  wire clock_1_out;

  Clock clock_1 (.out(clock_1_out));
  CPU cpu_1 (.Instruction(in_1), .Clk(clock_1_out));
endmodule

module CPU (
  input  [31:0] Instruction,
  input  Clk
);

  wire controllogic_1_aluarithmeticshift, controllogic_1_alusub, controllogic_1_useimm;
  wire [2:0] controllogic_1_aluop;
  wire [11:0] controllogic_1_imm;
  wire [31:0] alu_1_aluoutput, immgen_1_immout, multiplexer_1_out, registerfile_1_r1, registerfile_1_r2;

  ControlLogic controllogic_1 (
    .Instruction(Instruction), .ALUOp(controllogic_1_aluop), .Imm(controllogic_1_imm),
    .UseImm(controllogic_1_useimm), .ALUArithmeticShift(controllogic_1_aluarithmeticshift),
    .ALUSub(controllogic_1_alusub));
  RegisterFile registerfile_1 (
    .RS1(Instruction[19:15]), .RS2(Instruction[24:20]), .RD(Instruction[11:7]), .RD_Data(alu_1_aluoutput),
    .Clk(Clk), .R1(registerfile_1_r1), .R2(registerfile_1_r2));
  ImmGen immgen_1 (.ImmIn(controllogic_1_imm), .ImmOut(immgen_1_immout));
  Multiplexer #(.width(32)) multiplexer_1 (
    .in0(registerfile_1_r2), .in1(immgen_1_immout), .out(multiplexer_1_out), .sel(controllogic_1_useimm));
  ALU alu_1 (
    .RS1(registerfile_1_r1), .RS2(multiplexer_1_out), .ALUOperation(controllogic_1_aluop),
    .UseArithmeticRightShift(controllogic_1_aluarithmeticshift), .UseSubtract(controllogic_1_alusub),
    .ALUOutput(alu_1_aluoutput));
endmodule

module ALU (
  input  [31:0] RS1,
  input  [31:0] RS2,
  input  [2:0] ALUOperation,
  input  UseArithmeticRightShift,
  input  UseSubtract,
  output [31:0] ALUOutput
);

  wire comparator_1_lt, comparator_2_lt;
  wire [4:0] bit_extender_1_out, bit_extender_2_out;
  wire [31:0] adder_1_out, and_1_out, bit_extender_3_out, bit_extender_4_out, multiplexer_1_out,
       multiplexer_2_out, or_1_out, shifter_1_out, shifter_2_out, shifter_3_out, subtractor_1_out, xor_1_out;

  Bit_Extender #(.in_width(32), .out_width(5), .\type ("zero")) bit_extender_1 (.in(RS2), .out(bit_extender_1_out));
  Bit_Extender #(.in_width(32), .out_width(5), .\type ("zero")) bit_extender_2 (.in(RS2), .out(bit_extender_2_out));
  Shifter #(.width(32)) shifter_1 (.in(RS1), .\dist (bit_extender_1_out), .out(shifter_1_out));
  Adder #(.width(32)) adder_1 (.a(RS1), .b(RS2), .out(adder_1_out));  // open: cin, cout
  Subtractor #(.width(32)) subtractor_1 (.a(RS1), .b(RS2), .out(subtractor_1_out));  // open: bin, bout
  Comparator #(.width(32)) comparator_1 (.a(RS1), .b(RS2), .lt(comparator_1_lt));  // open: gt, eq
  Comparator #(.mode("unsigned"), .width(32)) comparator_2 (.a(RS1), .b(RS2), .lt(comparator_2_lt));  // open: gt, eq
  assign xor_1_out = RS1 ^ RS2;  // XOR_Gate xor_1, 32 bits wide
  assign or_1_out = RS1 | RS2;  // OR_Gate or_1, 32 bits wide
  assign and_1_out = RS1 & RS2;  // AND_Gate and_1, 32 bits wide
  Shifter #(.shift("lr"), .width(32)) shifter_2 (.in(RS1), .\dist (bit_extender_2_out), .out(shifter_2_out));
  Shifter #(.shift("ar"), .width(32)) shifter_3 (.in(RS1), .\dist (bit_extender_2_out), .out(shifter_3_out));
  Multiplexer #(.width(32)) multiplexer_1 (
    .in0(adder_1_out), .in1(subtractor_1_out), .out(multiplexer_1_out), .sel(UseSubtract));
  assign bit_extender_3_out = {{31{1'b0}}, comparator_1_lt};  // Bit_Extender bit_extender_3
  assign bit_extender_4_out = {{31{1'b0}}, comparator_2_lt};  // Bit_Extender bit_extender_4
  Multiplexer #(.width(32)) multiplexer_2 (
    .in0(shifter_2_out), .in1(shifter_3_out), .out(multiplexer_2_out), .sel(UseArithmeticRightShift));
  Multiplexer #(.select(3), .width(32)) multiplexer_3 (
    .in0(multiplexer_1_out), .in1(shifter_1_out), .in2(bit_extender_3_out), .in3(bit_extender_4_out),
    .in4(xor_1_out), .in5(multiplexer_2_out), .in6(or_1_out), .in7(and_1_out), .out(ALUOutput),
    .sel(ALUOperation));
endmodule

module RegisterFile (
  input  [4:0] RS1,
  input  [4:0] RS2,
  input  [4:0] RD,
  input  [31:0] RD_Data,
  input  Clk,
  output [31:0] R1,
  output [31:0] R2
);

  wire demultiplexer_1_out1, demultiplexer_1_out2, demultiplexer_1_out3, demultiplexer_1_out4,
       demultiplexer_1_out5, demultiplexer_1_out6, demultiplexer_1_out7, demultiplexer_1_out8,
       demultiplexer_1_out9, demultiplexer_1_out10, demultiplexer_1_out11, demultiplexer_1_out12,
       demultiplexer_1_out13, demultiplexer_1_out14, demultiplexer_1_out15, demultiplexer_1_out16,
       demultiplexer_1_out17, demultiplexer_1_out18, demultiplexer_1_out19, demultiplexer_1_out20,
       demultiplexer_1_out21, demultiplexer_1_out22, demultiplexer_1_out23, demultiplexer_1_out24,
       demultiplexer_1_out25, demultiplexer_1_out26, demultiplexer_1_out27, demultiplexer_1_out28,
       demultiplexer_1_out29, demultiplexer_1_out30, demultiplexer_1_out31;
  wire [31:0] register_1_q, register_2_q, register_3_q, register_4_q, register_5_q, register_6_q,
       register_7_q, register_8_q, register_9_q, register_10_q, register_11_q, register_12_q, register_13_q,
       register_14_q, register_15_q, register_16_q, register_17_q, register_18_q, register_19_q,
       register_20_q, register_21_q, register_22_q, register_23_q, register_24_q, register_25_q,
       register_26_q, register_27_q, register_28_q, register_29_q, register_30_q, register_31_q;

  Demultiplexer #(.select(5)) demultiplexer_1 (
    .out1(demultiplexer_1_out1), .out2(demultiplexer_1_out2), .out3(demultiplexer_1_out3),
    .out4(demultiplexer_1_out4), .out5(demultiplexer_1_out5), .out6(demultiplexer_1_out6),
    .out7(demultiplexer_1_out7), .out8(demultiplexer_1_out8), .out9(demultiplexer_1_out9),
    .out10(demultiplexer_1_out10), .out11(demultiplexer_1_out11), .out12(demultiplexer_1_out12),
    .out13(demultiplexer_1_out13), .out14(demultiplexer_1_out14), .out15(demultiplexer_1_out15),
    .out16(demultiplexer_1_out16), .out17(demultiplexer_1_out17), .out18(demultiplexer_1_out18),
    .out19(demultiplexer_1_out19), .out20(demultiplexer_1_out20), .out21(demultiplexer_1_out21),
    .out22(demultiplexer_1_out22), .out23(demultiplexer_1_out23), .out24(demultiplexer_1_out24),
    .out25(demultiplexer_1_out25), .out26(demultiplexer_1_out26), .out27(demultiplexer_1_out27),
    .out28(demultiplexer_1_out28), .out29(demultiplexer_1_out29), .out30(demultiplexer_1_out30),
    .out31(demultiplexer_1_out31), .in(1'b1), .sel(RD));  // open: out0
  Register #(.width(32)) register_1 (.D(RD_Data), .en(demultiplexer_1_out1), .clk(Clk), .Q(register_1_q));  // open: clr
  Register #(.width(32)) register_2 (.D(RD_Data), .en(demultiplexer_1_out2), .clk(Clk), .Q(register_2_q));  // open: clr
  Register #(.width(32)) register_3 (.D(RD_Data), .en(demultiplexer_1_out3), .clk(Clk), .Q(register_3_q));  // open: clr
  Register #(.width(32)) register_4 (.D(RD_Data), .en(demultiplexer_1_out4), .clk(Clk), .Q(register_4_q));  // open: clr
  Register #(.width(32)) register_5 (.D(RD_Data), .en(demultiplexer_1_out5), .clk(Clk), .Q(register_5_q));  // open: clr
  Register #(.width(32)) register_6 (.D(RD_Data), .en(demultiplexer_1_out6), .clk(Clk), .Q(register_6_q));  // open: clr
  Register #(.width(32)) register_7 (.D(RD_Data), .en(demultiplexer_1_out7), .clk(Clk), .Q(register_7_q));  // open: clr
  Register #(.width(32)) register_8 (.D(RD_Data), .en(demultiplexer_1_out8), .clk(Clk), .Q(register_8_q));  // open: clr
  Register #(.width(32)) register_9 (.D(RD_Data), .en(demultiplexer_1_out9), .clk(Clk), .Q(register_9_q));  // open: clr
  Register #(.width(32)) register_10 (
    .D(RD_Data), .en(demultiplexer_1_out10), .clk(Clk), .Q(register_10_q));  // open: clr
  Register #(.width(32)) register_11 (
    .D(RD_Data), .en(demultiplexer_1_out11), .clk(Clk), .Q(register_11_q));  // open: clr
  Register #(.width(32)) register_12 (
    .D(RD_Data), .en(demultiplexer_1_out12), .clk(Clk), .Q(register_12_q));  // open: clr
  Register #(.width(32)) register_13 (
    .D(RD_Data), .en(demultiplexer_1_out13), .clk(Clk), .Q(register_13_q));  // open: clr
  Register #(.width(32)) register_14 (
    .D(RD_Data), .en(demultiplexer_1_out14), .clk(Clk), .Q(register_14_q));  // open: clr
  Register #(.width(32)) register_15 (
    .D(RD_Data), .en(demultiplexer_1_out15), .clk(Clk), .Q(register_15_q));  // open: clr
  Register #(.width(32)) register_16 (
    .D(RD_Data), .en(demultiplexer_1_out16), .clk(Clk), .Q(register_16_q));  // open: clr
  Register #(.width(32)) register_17 (
    .D(RD_Data), .en(demultiplexer_1_out17), .clk(Clk), .Q(register_17_q));  // open: clr
  Register #(.width(32)) register_18 (
    .D(RD_Data), .en(demultiplexer_1_out18), .clk(Clk), .Q(register_18_q));  // open: clr
  Register #(.width(32)) register_19 (
    .D(RD_Data), .en(demultiplexer_1_out19), .clk(Clk), .Q(register_19_q));  // open: clr
  Register #(.width(32)) register_20 (
    .D(RD_Data), .en(demultiplexer_1_out20), .clk(Clk), .Q(register_20_q));  // open: clr
  Register #(.width(32)) register_21 (
    .D(RD_Data), .en(demultiplexer_1_out21), .clk(Clk), .Q(register_21_q));  // open: clr
  Register #(.width(32)) register_22 (
    .D(RD_Data), .en(demultiplexer_1_out22), .clk(Clk), .Q(register_22_q));  // open: clr
  Register #(.width(32)) register_23 (
    .D(RD_Data), .en(demultiplexer_1_out23), .clk(Clk), .Q(register_23_q));  // open: clr
  Register #(.width(32)) register_24 (
    .D(RD_Data), .en(demultiplexer_1_out24), .clk(Clk), .Q(register_24_q));  // open: clr
  Register #(.width(32)) register_25 (
    .D(RD_Data), .en(demultiplexer_1_out25), .clk(Clk), .Q(register_25_q));  // open: clr
  Register #(.width(32)) register_26 (
    .D(RD_Data), .en(demultiplexer_1_out26), .clk(Clk), .Q(register_26_q));  // open: clr
  Register #(.width(32)) register_27 (
    .D(RD_Data), .en(demultiplexer_1_out27), .clk(Clk), .Q(register_27_q));  // open: clr
  Register #(.width(32)) register_28 (
    .D(RD_Data), .en(demultiplexer_1_out28), .clk(Clk), .Q(register_28_q));  // open: clr
  Register #(.width(32)) register_29 (
    .D(RD_Data), .en(demultiplexer_1_out29), .clk(Clk), .Q(register_29_q));  // open: clr
  Register #(.width(32)) register_30 (
    .D(RD_Data), .en(demultiplexer_1_out30), .clk(Clk), .Q(register_30_q));  // open: clr
  Register #(.width(32)) register_31 (
    .D(RD_Data), .en(demultiplexer_1_out31), .clk(Clk), .Q(register_31_q));  // open: clr
  Multiplexer #(.select(5), .width(32)) multiplexer_1 (
    .in0({32{1'b0}}), .in1(register_1_q), .in2(register_2_q), .in3(register_3_q), .in4(register_4_q),
    .in5(register_5_q), .in6(register_6_q), .in7(register_7_q), .in8(register_8_q), .in9(register_9_q),
    .in10(register_10_q), .in11(register_11_q), .in12(register_12_q), .in13(register_13_q),
    .in14(register_14_q), .in15(register_15_q), .in16(register_16_q), .in17(register_17_q),
    .in18(register_18_q), .in19(register_19_q), .in20(register_20_q), .in21(register_21_q),
    .in22(register_22_q), .in23(register_23_q), .in24(register_24_q), .in25(register_25_q),
    .in26(register_26_q), .in27(register_27_q), .in28(register_28_q), .in29(register_29_q),
    .in30(register_30_q), .in31(register_31_q), .out(R1), .sel(RS1));
  Multiplexer #(.select(5), .width(32)) multiplexer_2 (
    .in0({32{1'b0}}), .in1(register_1_q), .in2(register_2_q), .in3(register_3_q), .in4(register_4_q),
    .in5(register_5_q), .in6(register_6_q), .in7(register_7_q), .in8(register_8_q), .in9(register_9_q),
    .in10(register_10_q), .in11(register_11_q), .in12(register_12_q), .in13(register_13_q),
    .in14(register_14_q), .in15(register_15_q), .in16(register_16_q), .in17(register_17_q),
    .in18(register_18_q), .in19(register_19_q), .in20(register_20_q), .in21(register_21_q),
    .in22(register_22_q), .in23(register_23_q), .in24(register_24_q), .in25(register_25_q),
    .in26(register_26_q), .in27(register_27_q), .in28(register_28_q), .in29(register_29_q),
    .in30(register_30_q), .in31(register_31_q), .out(R2), .sel(RS2));

  // Notes on the sheet:
  //   R0 is hard wired to 0
endmodule

module ControlLogic (
  input  [31:0] Instruction,
  output [2:0] ALUOp,
  output [11:0] Imm,
  output UseImm,
  output ALUArithmeticShift,
  output ALUSub
);

  Comparator #(.mode("unsigned"), .width(5)) comparator_1 (
    .a(Instruction[6:2]), .b(5'b00100), .eq(UseImm));  // open: gt, lt

  assign ALUArithmeticShift = Instruction[30];
  assign ALUOp = Instruction[14:12];
  assign ALUSub = Instruction[30];
  assign Imm = Instruction[31:20];
endmodule

module ImmGen (
  input  [11:0] ImmIn,
  output [31:0] ImmOut
);

  assign ImmOut = {{20{1'b0}}, ImmIn};  // Bit_Extender bit_extender_1
endmodule
